# Fritzing sketch esp_ikea_vindriktning (saved by Fritzing 0.9.3b)

parts:
  Espessif_Serial_Wifi_Modul_1 = ESP8266 ESP01 [part_number=ESP8266 package=THT]
  Composant2 = Adafruit 4-channel I2C-safe Bi-directional Logic Level Converter [part_number="Adafruit #757"]
  AMS1 = AMS1777 5V regulator module
  Power_plug1 = Power plug
  Composant3 = Adafruit SHT31-D [part_number="Adafruit #2857"]
  IC1 = ADS1115 16-bit ADC Breakout
  Composant4 = Adafruit CCS811 [part_number="Adafruit #3566"]
  Composant5 = Adafruit MiCS-5524 Gas Sensor [part_number="Adafruit #3199"]

nets:
  GND: Espessif_Serial_Wifi_Modul_1.GND, Composant2.GND, Composant3.GND, IC1.GND, Composant5.GND
  VCC: Espessif_Serial_Wifi_Modul_1.VCC, Espessif_Serial_Wifi_Modul_1.CH_PD, Composant2.LV, AMS1.VOUT+, Composant3.VCC, Composant4.VCC
  N1: Espessif_Serial_Wifi_Modul_1.GPIO00, Composant2.A1, Composant4.SCL
  N2: Espessif_Serial_Wifi_Modul_1.GPIO02, Composant2.A2
  N3: Composant2.B2, IC1.SDA
  N4: Composant2.B1, IC1.SCL
  VCC_2: Composant2.HV, AMS1.VIN+, Power_plug1.VCC, IC1.VDD, Composant5.5.0V
  N5: AMS1.GND-_(input), Power_plug1.GND
  N6: AMS1.GND-_(output), Composant4.GND
  N7: Composant3.SDA, Composant4.SDA
  N8: IC1.A0, Composant5.AOUT

notes:
  ESP8266 esp01s /esphome
  5V
  3.3V
  AMS1117
  5V pm1006 board
  Level Shifter

custom parts:
  ESP8266 ESP01: Generic WiFi Module based on the ESP8266 with onboard PCB antenna and UART communications
  Adafruit 4-channel I2C-safe Bi-directional Logic Level Converter: Because the Arduino (and Basic Stamp) are 5V devices, and most modern sensors, displays, flash cards and modes are 3.3V-only, many makers find that they need to perform level shifting/conversion to protect the 3.3V device from 5V. We do have some other handy level shifters in the shop, from the DIP 74LVC245 to the fancy bi-directional TXB0108. However, neither of these are happy to work with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
  AMS1777 5V regulator module: AMS1777 5V regulator module source : https://github.com/ShenTengTu/fritzing_parts/tree/master/voltage%20regulator/AMS1117_5V_regulator_module
  Adafruit SHT31-D: Sensirion Temperature/Humidity sensors are some of the finest & highest-accuracy devices you can get. And, finally we have some that have a true I2C interface for easy reading. The SHT31-D sensor has an excellent ±2% relative humidity and ±0.3°C accuracy for most uses. We now use the version with a PTFE filter, it'll stay clean while still allowing humidity measurements to work Unlike earlier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
  ADS1115 16-bit ADC Breakout: ADS1015 12-bit I2C ADC+PGA Breakout
  Adafruit CCS811: Breathe easy - we finally have an I2C VOC/eCO2 sensor in the Adafruit shop! Add air quality monitoring to your project and with an Adafruit CCS811 Air Quality Sensor Breakout. This sensor from AMS is a gas sensor that can detect a wide range of Volatile Organic Compounds (VOCs) and is intended for indoor air quality monitoring. When connected to your microcontroller (running our library code)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
  Adafruit MiCS-5524 Gas Sensor: Give your next sensor project a nose for gasses with the Adafruit MiCS-5524 Gas Sensor Breakout. This breakout makes it easy to use this nice sensor from SGX Sensortech. The MiCS-5524 is a robust MEMS sensor for indoor carbon monoxide and natural gas leakage detection, it's suitable also for indoor air quality monitoring; breath checker and early fire detection. Please note: This sensor is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
